// Logisim project mux.circ as structural Verilog: 2 circuits, main circuit mux1bitconE
module mux1bit (
  input  I0,
  input  I1,
  input  S,
  output Y
);

  wire and_1_out, and_2_out, not_1_out;

  not not_1 (not_1_out, S);
  and and_1 (and_1_out, I0, not_1_out);
  and and_2 (and_2_out, I1, S);
  or or_1 (Y, and_1_out, and_2_out);
endmodule

module mux1bitconE (
  input  I0,
  input  I1,
  input  S,
  input  E,
  output Y
);

  wire and_1_out, and_2_out, not_1_out;

  not not_1 (not_1_out, S);
  and and_1 (and_1_out, I0, E, not_1_out);
  and and_2 (and_2_out, I1, E, S);
  or or_1 (Y, and_1_out, and_2_out);
endmodule
