// Logisim project restador.circ as structural Verilog
module restadorSimple (
  input  A,
  input  B,
  output R,
  output P
);

  xor xor_1 (R, A, B);
  and and_1 (P, ~A, B);  // AND_Gate
endmodule
