// Logisim project restadorCompleto.circ as structural Verilog: 3 circuits, main circuit restadorCompletoXor
module restadorCompletoXor (
  input  A,
  input  B,
  input  Pi,
  output R,
  output Pout
);

  wire and_1_out, and_2_out, and_3_out, not_1_out, xor_1_out;

  not not_1 (not_1_out, A);
  and and_1 (and_1_out, not_1_out, B);
  and and_2 (and_2_out, not_1_out, Pi);
  and and_3 (and_3_out, B, Pi);
  xor xor_1 (xor_1_out, B, Pi);
  or or_1 (Pout, and_1_out, and_2_out, and_3_out);
  xor xor_2 (R, A, xor_1_out);
endmodule

module restador1bit (
  input  A,
  input  B,
  input  Pi,
  output Pout,
  output R
);

  wire and_1_out, and_2_out, and_3_out, and_4_out, and_5_out, and_6_out, and_7_out, not_1_out, not_2_out,
       not_3_out;

  not not_1 (not_1_out, A);
  not not_2 (not_2_out, B);
  not not_3 (not_3_out, Pi);
  and and_1 (and_1_out, not_1_out, Pi);
  and and_2 (and_2_out, not_1_out, B);
  and and_3 (and_3_out, B, Pi);
  and and_4 (and_4_out, not_1_out, not_2_out, Pi);
  and and_5 (and_5_out, not_1_out, B, not_3_out);
  and and_6 (and_6_out, A, not_2_out, not_3_out);
  and and_7 (and_7_out, A, B, Pi);
  or or_1 (Pout, and_1_out, and_2_out, and_3_out);
  or or_2 (R, and_4_out, and_5_out, and_6_out, and_7_out);
endmodule

module restador4bits (
  input  A3,
  input  A2,
  input  A1,
  input  A0,
  input  B3,
  input  B2,
  input  B1,
  input  B0,
  output R3,
  output R2,
  output R1,
  output R0
);

  wire restadorcompletoxor_1_pout, restadorcompletoxor_2_pout, restadorcompletoxor_3_pout;

  restadorCompletoXor restadorcompletoxor_1 (.R(R0), .Pout(restadorcompletoxor_1_pout), .A(A0), .B(B0), .Pi(1'b0));
  restadorCompletoXor restadorcompletoxor_2 (
    .R(R1), .Pout(restadorcompletoxor_2_pout), .A(A1), .B(B1), .Pi(restadorcompletoxor_1_pout));
  restadorCompletoXor restadorcompletoxor_3 (
    .R(R2), .Pout(restadorcompletoxor_3_pout), .A(A2), .B(B2), .Pi(restadorcompletoxor_2_pout));
  restadorCompletoXor restadorcompletoxor_4 (.R(R3), .A(A3), .B(B3), .Pi(restadorcompletoxor_3_pout));  // open: Pout

  // Notes on the sheet:
  //   -
endmodule
